# Fritzing sketch lisakeys (saved by Fritzing 0.9.2b)
circuit board: 6.88566cm x 5.36311cm
breadboards: 1

parts:
  J1 = female pin header, 8 pins [form="♀ (female)"]
  J2 = female pin header, 10 pins [form="♀ (female)"]
  J3 = female pin header, 6 pins [form="♀ (female)"]
  J4 = female pin header, 8 pins [form="♀ (female)"]
  J5 = female pin header, 1 pin [form="♀ (female)"]  # not connected
  J6 = female pin header, 1 pin [form="♀ (female)"]  # not connected
  J7 = female pin header, 1 pin [form="♀ (female)"]  # not connected
  J8 = female pin header, 1 pin [form="♀ (female)"]
  J9 = female pin header, 1 pin [form="♀ (female)"]
  J10 = female pin header, 1 pin [form="♀ (female)"]
  1 = Pushbutton [package="[THT]"]
  2 = Pushbutton [package="[THT]"]
  3 = Pushbutton [package="[THT]"]
  S = Pushbutton [package="[THT]"]
  part = Pushbutton [package="[THT]"]
  CR = Pushbutton [package="[THT]"]
  SH = Pushbutton [package="[THT]"]
  AP = Pushbutton [package="[THT]"]
  SP = Pushbutton [package="[THT]"]
  D2 = Diode [package=diode-1n4148]
  D3 = Diode [package=diode-1n4148]
  D4 = Diode [package=diode-1n4148]
  D5 = Diode [package=diode-1n4148]
  D6 = Diode [package=diode-1n4148]
  D7 = Diode [package=diode-1n4148]
  D8 = Diode [package=diode-1n4148]
  D9 = Diode [package=diode-1n4148]
  D10 = Diode [package=diode-1n4148]
  S1 = Toggle Switch [package=THT]
  S2 = Toggle Switch [package=THT]
  S3 = Toggle Switch [package=THT]
  S4 = Toggle Switch [package=THT]
  S5 = Toggle Switch [package=THT]
  S6 = Toggle Switch [package=THT]
  S7 = Toggle Switch [package=THT]
  S8 = Pushbutton [package="[THT]"]

nets:
  N1: J1.pin2, J9.pin1
  N2: J1.pin3, S1.L1, S1.COM
  N3: J1.pin4, S2.L1, S2.COM
  N4: J1.pin5, S3.L1, S3.COM
  N5: J1.pin6, S4.L1, S4.COM
  N6: J1.pin7, S5.L1, S5.COM
  N7: J1.pin8, S6.L1, S6.COM
  N8: J2.pin4, J8.pin1, S1.L2, S2.L2, S3.L2, S4.L2, S5.L2, S6.L2, S8.Pin_3, S8.Pin_4
  N9: J3.pin1, 1.Pin_1, 1.Pin_2, 2.Pin_1, 2.Pin_2, 3.Pin_1, 3.Pin_2
  N10: J3.pin2, S.Pin_1, S.Pin_2, part.Pin_1, part.Pin_2, CR.Pin_1, CR.Pin_2
  N11: J3.pin3, SH.Pin_1, SH.Pin_2, AP.Pin_1, AP.Pin_2, SP.Pin_1, SP.Pin_2
  N12: J3.pin4, D2.C, D5.C, D8.C
  N13: J3.pin5, D3.C, D6.C, D9.C
  N14: J3.pin6, D4.C, D7.C, D10.C
  N15: J4.pin3, S8.Pin_1, S8.Pin_2
  N16: J4.pin5, S7.L1
  N17: J4.pin8, S7.L2
  N18: J10.pin1, S7.COM
  N19: 1.Pin_3, 1.Pin_4, D2.A
  N20: 2.Pin_3, 2.Pin_4, D3.A
  N21: 3.Pin_3, 3.Pin_4, D4.A
  N22: S.Pin_3, S.Pin_4, D5.A
  N23: part.Pin_3, part.Pin_4, D6.A
  N24: CR.Pin_3, CR.Pin_4, D7.A
  N25: SH.Pin_3, SH.Pin_4, D8.A
  N26: AP.Pin_3, AP.Pin_4, D9.A
  N27: SP.Pin_3, SP.Pin_4, D10.A

notes:
  RESET
  KBD
  5V
  Vin
  1
  2
  3
  S
  .
  Return
  Shift
  Apple
  Space
  PWR
  >LH
  LK>
  USB
  SER
  MAC
  DE/FR
  PC
  US/UK
  MIR
  UK/FR
  LFT
  US/DE
  |-USB>LH-|
  A
  B
  C
  D
  E
  F
  Keyboard
  Tester/
  Translator/
  Emulator
  LFK
  MFK
